# Fritzing sketch schematic (saved by Fritzing 0.9.3b)

parts:
  U1 = ESP32-38PinWide [part_number=ESP32-38PinWide]
  R1 = Resistor [tolerance=±5% resistance=220 package=THT]
  J1 = Basic Servo
  U2 = SWITCH_SPDT [package=kps-1290]
  M1 = DC Motor  # not connected
  M2 = DC Motor
  S1 = H-Bridge with L298N
  BAT3 = 18650 battery holder [package=battery-18650-kit]
  BAT4 = 18650 battery holder [package=battery-18650-kit]
  BAT7 = 18650 battery holder [package=battery-18650-kit]
  BAT8 = 18650 battery holder [package=battery-18650-kit]
  U4 = Voltage Regulator - 5V [package="TO220 [THT]"]
  M3 = fc-51 [package=THT]
  M4 = fc-51 [package=THT]
  R2 = Resistor [tolerance=±5% resistance=220 package=THT]  # not connected

nets:
  N1: U1.3.3, U2.O
  N2: U1.GPIO32, S1.ENB
  N3: U1.GPIO33, S1.IN4
  N4: U1.GPIO25, S1.IN3
  N5: U1.GPIO26, S1.IN2
  N6: U1.GPIO27, S1.IN1
  N7: U1.GPIO14, S1.ENA
  N8: U1.GPIO16, M3.pin1
  N9: U1.GPIO17, M4.pin1
  N10: U1.GND, R1.Pin_1
  N11: R1.Pin_0, U2.P
  N12: J1.vcc, U4.output_voltage
  N13: M2.pin_1, S1.M1-02
  N14: M2.pin_2, S1.M1-01
  N15: S1.12V, BAT4.+
  N16: S1.GND, BAT3.-
  N17: BAT3.+, BAT4.-
  N18: BAT7.+, U4.input_voltage
  N19: BAT7.-, BAT8.+
  N20: BAT8.-, U4.GND

custom parts:
  ESP32-38PinWide: Generic 38-Pin ESP32 with wide format (only access to one side of pins on a breadboard) based on Stephen Lilley's HiLetgo ESP-WROOM-32 ESP32 ESP-32S Development Board.
  H-Bridge with L298N: h-bridge
  18650 battery holder: 18650 Battery Holder
